// Logisim project ULA+Teclado.circ as structural Verilog: 1 circuit, main circuit main
// zera
module main (
  input  in_1,
  input  in_2,
  output out_3
);

  wire a1, and_2_out, and_3_out, and_4_out, and_5_out, and_6_out, apagar_teclado, apagar_tela, \botão_1 ,
       clock_1_out, clock_2_out, clock_3_out, comparator_1_eq, comparator_2_eq, comparator_3_eq,
       comparator_4_eq, comparator_5_eq, comparator_6_eq, comparator_7_gt, comparator_7_lt, contador_ram,
       counter_5_carry, counter_6_carry, enviar, Ligar, load, not_1_out, not_2_out, not_3_out, not_4_out,
       or_1_out, or_2_out, or_5_out, or_6_out, parar_comparador, register_2_q, reiniciar,
       verifica_meu_nome_e, verifica_oi, zera, zera_meu_nome_e, zera_oi;
  wire [2:0] counter_2_q, teste;
  wire [3:0] counter_1_q, counter_4_q, counter_5_q, counter_6_q, multiplexer_4_out, Nome;
  wire [4:0] counter_8_q;
  wire [6:0] buffer_1_out, \input , meu_nome_e, multiplexer_1_out, multiplexer_2_out, oi, \output , ram_oi,
       rom_1_data, rom_3_data, rom_4_data, saida_RAM, saidaRam2;

  Keyboard keyboard_1 (.clk(\botão_1 ), .re(Ligar), .clr(apagar_teclado), .avail(a1), .data(\input ));
  Clock clock_1 (.out(clock_1_out));
  Register #(.width(1)) register_1 (.D(enviar), .Q(Ligar), .clk(enviar), .clr(zera));  // open: en
  or or_1 (or_1_out, not_1_out, zera);
  not not_1 (not_1_out, Ligar);
  not not_2 (not_2_out, Ligar);
  and and_1 (\botão_1 , Ligar, clock_1_out);
  Counter #(.width(4), .max('hf)) counter_1 (
    .load(in_1), .Q(counter_1_q), .clk(\botão_1 ), .clr(or_1_out));  // open: D, count, carry
  Counter #(.width(3), .max('h3)) counter_2 (
    .load(in_2), .Q(counter_2_q), .clk(\botão_1 ), .clr(or_2_out));  // open: D, count, carry
  or or_2 (or_2_out, not_2_out, zera);
  Comparator #(.width(7)) comparator_1 (.a(\input ), .b(7'b0001010), .eq(comparator_1_eq));  // open: gt, lt
  Comparator #(.width(7)) comparator_2 (.a(\output ), .b(7'b0001010), .eq(comparator_2_eq));  // open: gt, lt
  Multiplexer #(.width(7), .enable("false")) multiplexer_1 (
    .in0(\input ), .in1(oi), .out(multiplexer_1_out), .sel(verifica_oi));
  Multiplexer #(.width(7), .enable("false")) multiplexer_2 (
    .in0(multiplexer_1_out), .in1(meu_nome_e), .out(multiplexer_2_out), .sel(verifica_meu_nome_e));
  assign buffer_1_out = \input ;  // Buffer buffer_1, 7 bits wide
  not not_3 (not_3_out, Ligar);
  Button button_1 (.out(enviar));
  Button button_2 (.out(apagar_tela));
  Button button_3 (.out(reiniciar));
  Button button_4 (.out(apagar_teclado));
  D_Flip_Flop d_ff_1 (.clk(comparator_1_eq), .D(comparator_1_eq), .Q(load), .reset(zera));  // open: Qn, preset, en
  and and_2 (and_2_out, comparator_2_eq, verifica_oi);
  TTY tty_1 (.data(multiplexer_2_out), .clk(\botão_1 ), .we(\botão_1 ), .clr(apagar_tela));
  not not_4 (not_4_out, parar_comparador);
  or or_3 (contador_ram, not_3_out, zera);
  ROM #(.addrWidth(4), .dataWidth(7)) rom_1 (.addr(counter_1_q), .data(rom_1_data));  // open: sel
  ROM #(.addrWidth(3), .dataWidth(7)) rom_2 (.addr(counter_2_q), .data(ram_oi));  // open: sel
  D_Flip_Flop d_ff_2 (.clk(and_2_out), .D(and_2_out), .Q(out_3), .reset(zera));  // open: Qn, preset, en
  Counter #(.width(5), .max('h1f), .ongoal("stay")) counter_3 (
    .carry(parar_comparador), .clk(\botão_1 ), .clr(zera));  // open: load, D, count, Q
  Counter #(.width(4), .max('hf)) counter_4 (
    .count(not_4_out), .Q(counter_4_q), .clk(\botão_1 ), .clr(contador_ram));  // open: load, D, carry
  Comparator #(.width(7)) comparator_3 (.a(rom_1_data), .b(saidaRam2), .eq(comparator_3_eq));  // open: gt, lt
  Counter #(.width(4), .max('hf), .ongoal("stay")) counter_5 (
    .Q(counter_5_q), .carry(counter_5_carry), .clk(comparator_3_eq), .clr(zera));  // open: load, D, count
  RAM #(.addrWidth(4), .dataWidth(7), .bus("separate")) ram_1 (
    .addr(counter_4_q), .din(buffer_1_out), .data(saida_RAM), .str(a1), .clk(\botão_1 ), .ld(load),
    .clr(contador_ram));  // open: sel
  Multiplexer #(.width(4), .enable("false")) multiplexer_3 (
    .in0(4'b0000), .in1(counter_5_q), .out(Nome), .sel(counter_5_carry));
  Counter #(.width(4), .max('hf), .ongoal("stay")) counter_6 (
    .Q(counter_6_q), .carry(counter_6_carry), .clk(comparator_4_eq), .clr(zera));  // open: load, D, count
  Comparator #(.width(7)) comparator_4 (.a(saidaRam2), .b(ram_oi), .eq(comparator_4_eq));  // open: gt, lt
  or or_4 (zera, reiniciar, zera_meu_nome_e, zera_oi);
  Comparator #(.width(7)) comparator_5 (.a(saida_RAM), .b(7'b0001010), .eq(comparator_5_eq));  // open: gt, lt
  Multiplexer #(.width(4), .enable("false")) multiplexer_4 (
    .in0(4'b0000), .in1(counter_6_q), .out(multiplexer_4_out), .sel(counter_6_carry));
  Comparator #(.width(7)) comparator_6 (.a(oi), .b({7{1'b0}}), .eq(comparator_6_eq));  // open: gt, lt
  Register #(.width(1)) register_2 (
    .D(comparator_5_eq), .Q(register_2_q), .clk(comparator_5_eq), .clr(zera));  // open: en
  Comparator #(.width(4)) comparator_7 (
    .a(Nome), .b(multiplexer_4_out), .gt(comparator_7_gt), .lt(comparator_7_lt));  // open: eq
  Clock clock_2 (.out(clock_2_out));
  Clock clock_3 (.out(clock_3_out));
  Multiplexer #(.width(7), .enable("false")) multiplexer_5 (
    .in1(saida_RAM), .out(saidaRam2), .sel(register_2_q));  // open: in0
  and and_3 (and_3_out, comparator_6_eq, or_5_out);
  or or_5 (or_5_out, zera_oi, zera_meu_nome_e);
  and and_4 (and_4_out, verifica_oi, clock_2_out);
  and and_5 (and_5_out, verifica_oi, and_3_out);
  and and_6 (and_6_out, verifica_meu_nome_e, clock_3_out);
  Register #(.width(1)) register_3 (
    .D(comparator_7_gt), .Q(verifica_oi), .clk(comparator_7_gt), .clr(or_6_out));  // open: en
  or or_6 (or_6_out, zera, and_5_out);
  Counter #(.width(3), .max('h4), .ongoal("stay")) counter_7 (
    .Q(teste), .clk(and_4_out), .clr(zera));  // open: load, D, count, carry
  Counter #(.width(5), .max('h10), .ongoal("stay")) counter_8 (
    .Q(counter_8_q), .clk(and_6_out), .clr(zera));  // open: load, D, count, carry
  Register #(.width(1)) register_4 (
    .D(comparator_7_lt), .Q(verifica_meu_nome_e), .clk(comparator_7_lt), .clr(zera));  // open: en
  ROM #(.addrWidth(3), .dataWidth(7)) rom_3 (.addr(teste), .data(rom_3_data));  // open: sel
  ROM #(.addrWidth(5), .dataWidth(7)) rom_4 (.addr(counter_8_q), .data(rom_4_data));  // open: sel
  Comparator #(.width(7)) comparator_8 (.a({7{1'b0}}), .b(rom_3_data), .eq(zera_oi));  // open: gt, lt
  Multiplexer #(.width(7), .enable("false")) multiplexer_6 (.in0(rom_3_data), .out(oi), .sel(zera_oi));  // open: in1
  Comparator #(.width(7)) comparator_9 (.a({7{1'b0}}), .b(rom_4_data), .eq(zera_meu_nome_e));  // open: gt, lt
  Multiplexer #(.width(7), .enable("false")) multiplexer_7 (
    .in0(rom_4_data), .in1({7{1'b0}}), .out(meu_nome_e), .sel(zera_meu_nome_e));

  // Other names for the same wires on the sheet: zera_o_clock_oi = verifica_oi

  // Notes on the sheet:
  //   Oi
  //   Qual o seu nome
  //   Enviar
  //   Apagar Tela
  //   Reiniciar Circuito
  //   Apagar Teclado
  //   Palavras para comparar
  //   contents of rom_1 (hex, n*v repeats v):
  //   71 75 61 6c 20 6f 20 73 65 75 20 6e 6f 6d 65 a
  //   contents of rom_2 (hex, n*v repeats v):
  //   6f 69 a
  //   Zera os clocks
  //   Oi
  //   Meu nome e Ana
  //   Respostas do bot
  //   contents of rom_3 (hex, n*v repeats v):
  //   11 6f 69 a
  //   contents of rom_4 (hex, n*v repeats v):
  //   11 6d 65 75 20 6e 6f 6d 65 20 65 20 61 6e 61 a
endmodule
